// Logisim project TP 2.circ as structural Verilog: 10 circuits, main circuit main
module main (
  input  A0,
  input  A1,
  input  Cin,
  input  A2,
  input  A3,
  input  B0,
  input  B1,
  input  B2,
  input  B3
);

  wire decodificador_1_a, decodificador_1_b, decodificador_1_c, decodificador_1_d, decodificador_1_e,
       decodificador_1_f, decodificador_1_g, decodificador_1_h, decodificador_2_a, decodificador_2_b,
       decodificador_2_c, decodificador_2_d, decodificador_2_e, decodificador_2_f, decodificador_2_g,
       decodificador_2_h, decodificador_3_a, decodificador_3_b, decodificador_3_c, decodificador_3_d,
       decodificador_3_e, decodificador_3_f, decodificador_3_g, decodificador_3_h, somador4_1_cout,
       somador4_1_of, somador4_1_s0, somador4_1_s1, somador4_1_s2, somador4_1_s3;

  Decodificador decodificador_1 (
    .X0(A0), .X1(A1), .X2(A2), .X3(A3), .A(decodificador_1_a), .B(decodificador_1_b), .C(decodificador_1_c),
    .D(decodificador_1_d), .E(decodificador_1_e), .F(decodificador_1_f), .G(decodificador_1_g),
    .H(decodificador_1_h));
  Somador4 somador4_1 (
    .A0(A0), .A1(A1), .A2(A2), .A3(A3), .B0(B0), .B1(B1), .B2(B2), .B3(B3), .Cin(Cin),
    .Cout(somador4_1_cout), .S0(somador4_1_s0), .S1(somador4_1_s1), .S2(somador4_1_s2), .S3(somador4_1_s3),
    .OF(somador4_1_of));
  LED Cout (.in(somador4_1_cout));
  Decodificador decodificador_2 (
    .X0(B0), .X1(B1), .X2(B2), .X3(B3), .A(decodificador_2_a), .B(decodificador_2_b), .C(decodificador_2_c),
    .D(decodificador_2_d), .E(decodificador_2_e), .F(decodificador_2_f), .G(decodificador_2_g),
    .H(decodificador_2_h));
  _7_Segment_Display u_7_segment_display_1 (
    .g(decodificador_1_d), .f(decodificador_1_c), .a(decodificador_1_b), .b(decodificador_1_a),
    .e(decodificador_1_e), .d(decodificador_1_f), .c(decodificador_1_g), .dp(decodificador_1_h));
  _7_Segment_Display u_7_segment_display_2 (
    .g(decodificador_2_d), .f(decodificador_2_c), .a(decodificador_2_b), .b(decodificador_2_a),
    .e(decodificador_2_e), .d(decodificador_2_f), .c(decodificador_2_g), .dp(decodificador_2_h));
  LED S0 (.in(somador4_1_s0));
  LED S1 (.in(somador4_1_s1));
  LED S2 (.in(somador4_1_s2));
  LED S3 (.in(somador4_1_s3));
  LED OF (.in(somador4_1_of));
  Decodificador decodificador_3 (
    .X0(somador4_1_s0), .X1(somador4_1_s1), .X2(somador4_1_s2), .X3(somador4_1_s3), .A(decodificador_3_a),
    .B(decodificador_3_b), .C(decodificador_3_c), .D(decodificador_3_d), .E(decodificador_3_e),
    .F(decodificador_3_f), .G(decodificador_3_g), .H(decodificador_3_h));
  _7_Segment_Display u_7_segment_display_3 (
    .g(decodificador_3_d), .f(decodificador_3_c), .a(decodificador_3_b), .b(decodificador_3_a),
    .e(decodificador_3_e), .d(decodificador_3_f), .c(decodificador_3_g), .dp(decodificador_3_h));
endmodule

module ULA1 (
  input  Binvert,
  input  Cin,
  input  OP1,
  input  OP0,
  input  A,
  input  B,
  output S,
  output Cout
);

  wire and_1_out, multiplex1_1_s, not_1_out, not_2_out, or_1_out, somador1_1_s;

  Multiplex1 multiplex1_1 (.A(B), .B(not_1_out), .OP(Binvert), .S(multiplex1_1_s));
  not not_1 (not_1_out, B);
  and and_1 (and_1_out, A, multiplex1_1_s);
  or or_1 (or_1_out, A, multiplex1_1_s);
  not not_2 (not_2_out, A);
  Somador1 somador1_1 (.A(A), .B(multiplex1_1_s), .Cin(Cin), .Cout(Cout), .S(somador1_1_s));
  Multiplex4 multiplex4_1 (.A(and_1_out), .B(or_1_out), .C(not_2_out), .D(somador1_1_s), .OP1(OP1), .OP0(OP0), .S(S));
endmodule

module ULA4 (
  input  B3,
  input  B2,
  input  B1,
  input  B0,
  input  A3,
  input  A2,
  input  A1,
  input  A0,
  input  Binvert,
  input  OP1,
  input  OP0,
  output S0,
  output S1,
  output S2,
  output S3,
  output Cout
);

  wire ula1_1_cout, ula1_2_cout, ula1_3_cout;

  ULA1 ula1_1 (.A(A0), .B(B0), .Binvert(Binvert), .Cin(Binvert), .OP1(OP1), .OP0(OP0), .Cout(ula1_1_cout), .S(S0));
  ULA1 ula1_2 (.A(A1), .B(B1), .Binvert(Binvert), .Cin(ula1_1_cout), .OP1(OP1), .OP0(OP0), .Cout(ula1_2_cout), .S(S1));
  ULA1 ula1_3 (.A(A2), .B(B2), .Binvert(Binvert), .Cin(ula1_2_cout), .OP1(OP1), .OP0(OP0), .Cout(ula1_3_cout), .S(S2));
  ULA1 ula1_4 (.A(A3), .B(B3), .Binvert(Binvert), .Cin(ula1_3_cout), .OP1(OP1), .OP0(OP0), .Cout(Cout), .S(S3));
endmodule

module Multiplex1 (
  input  OP,
  input  A,
  input  B,
  output S
);

  wire and_1_out, and_2_out, not_1_out;

  not not_1 (not_1_out, OP);
  and and_1 (and_1_out, not_1_out, A);
  and and_2 (and_2_out, OP, B);
  or or_1 (S, and_1_out, and_2_out);
endmodule

module Multiplex4 (
  input  OP1,
  input  OP0,
  input  A,
  input  B,
  input  C,
  input  D,
  output S
);

  wire and_1_out, and_2_out, and_3_out, and_4_out, not_1_out, not_2_out, not_3_out, not_4_out;

  not not_1 (not_1_out, OP0);
  not not_2 (not_2_out, OP1);
  and and_1 (and_1_out, not_1_out, not_2_out, A);
  not not_3 (not_3_out, OP1);
  and and_2 (and_2_out, OP0, not_3_out, B);
  not not_4 (not_4_out, OP0);
  and and_3 (and_3_out, not_4_out, OP1, C);
  and and_4 (and_4_out, OP0, OP1, D);
  or or_1 (S, and_1_out, and_2_out, and_3_out, and_4_out);
endmodule

module Somador1 (
  input  Cin,
  input  A,
  input  B,
  output S,
  output Cout
);

  wire and_1_out, and_2_out, xor_1_out;

  and and_1 (and_1_out, A, B);
  xor xor_1 (xor_1_out, A, B);
  xor xor_2 (Cout, and_1_out, and_2_out);
  and and_2 (and_2_out, xor_1_out, Cin);
  xor xor_3 (S, Cin, xor_1_out);
endmodule

module Somador4 (
  input  Cin,
  input  A0,
  input  A1,
  input  A2,
  input  A3,
  input  B0,
  input  B1,
  input  B2,
  input  B3,
  output S0,
  output S1,
  output S2,
  output S3,
  output OF,
  output Cout
);

  wire somador1_1_cout, somador1_2_cout, somador1_3_cout;

  Somador1 somador1_1 (.A(A0), .B(B0), .Cin(Cin), .Cout(somador1_1_cout), .S(S0));
  Somador1 somador1_2 (.A(A1), .B(B1), .Cin(somador1_1_cout), .Cout(somador1_2_cout), .S(S1));
  Somador1 somador1_3 (.A(A2), .B(B2), .Cin(somador1_2_cout), .Cout(somador1_3_cout), .S(S2));
  Somador1 somador1_4 (.A(A3), .B(B3), .Cin(somador1_3_cout), .Cout(Cout), .S(S3));

  assign OF = Cout;
endmodule

module _1_2_Somador (
  input  A,
  input  B,
  output S,
  output Cout
);

  xor xor_1 (S, A, B);
  and and_1 (Cout, A, B);
endmodule

module _2_1_2_Somador (
  input  A,
  input  B,
  input  B_2,
  output S,
  output Cout
);

  wire and_1_out, and_2_out, xor_1_out;

  xor xor_1 (xor_1_out, A, B);
  and and_1 (and_1_out, A, B);
  xor xor_2 (S, xor_1_out, B_2);
  and and_2 (and_2_out, xor_1_out, B_2);
  or or_1 (Cout, and_2_out, and_1_out);
endmodule

module Decodificador (
  input  X0,
  input  X1,
  input  X2,
  input  X3,
  output A,
  output B,
  output C,
  output D,
  output E,
  output F,
  output G,
  output H
);

  wire and_1_out, and_2_out, and_3_out, and_4_out, and_5_out, and_6_out, and_7_out, and_8_out, and_9_out,
       and_10_out, and_11_out, and_12_out, and_13_out, and_14_out, and_15_out, and_16_out, and_17_out,
       and_18_out, and_19_out, and_20_out, and_21_out, and_22_out, and_23_out, and_24_out, and_25_out,
       and_26_out, and_27_out, and_28_out, and_29_out, and_30_out, and_31_out, and_32_out, and_33_out,
       and_34_out, and_35_out, not_1_out, not_2_out, not_3_out, not_4_out, not_5_out, not_6_out, not_7_out,
       not_8_out, not_9_out, not_10_out, not_11_out, not_12_out, not_13_out, not_14_out, not_15_out,
       not_16_out, not_17_out, not_18_out, not_19_out, not_20_out, not_21_out, not_22_out, not_23_out,
       not_24_out, not_25_out, not_26_out, not_27_out, not_28_out, not_29_out, not_30_out, not_31_out,
       not_32_out, not_33_out, not_34_out, not_35_out, not_36_out, not_37_out, not_38_out, not_39_out,
       not_40_out, not_41_out, not_42_out, not_43_out;

  not not_1 (not_1_out, X0);
  not not_2 (not_2_out, X1);
  and and_1 (and_1_out, not_1_out, not_2_out, not_3_out);
  not not_3 (not_3_out, X3);
  not not_4 (not_4_out, X0);
  and and_2 (and_2_out, not_4_out, not_5_out);
  not not_5 (not_5_out, X2);
  not not_6 (not_6_out, X1);
  and and_3 (and_3_out, not_6_out, not_7_out);
  not not_7 (not_7_out, X2);
  and and_4 (and_4_out, X0, not_8_out, X3);
  not not_8 (not_8_out, X1);
  and and_5 (and_5_out, X0, X1, not_9_out);
  not not_9 (not_9_out, X3);
  not not_10 (not_10_out, X0);
  and and_6 (and_6_out, not_10_out, not_11_out);
  not not_11 (not_11_out, X2);
  not not_12 (not_12_out, X0);
  and and_7 (and_7_out, not_12_out, X3);
  not not_13 (not_13_out, X1);
  and and_8 (and_8_out, not_13_out, not_14_out, X3);
  not not_14 (not_14_out, X2);
  and and_9 (and_9_out, X1, not_15_out);
  not not_15 (not_15_out, X3);
  and and_10 (and_10_out, X1, X2);
  and and_11 (and_11_out, X0, X2, not_16_out);
  not not_16 (not_16_out, X3);
  not not_17 (not_17_out, X0);
  and and_12 (and_12_out, not_17_out, not_18_out);
  not not_18 (not_18_out, X1);
  not not_19 (not_19_out, X2);
  and and_13 (and_13_out, not_19_out, X3);
  not not_20 (not_20_out, X0);
  and and_14 (and_14_out, not_20_out, X2);
  not not_21 (not_21_out, X1);
  and and_15 (and_15_out, not_21_out, X2, not_22_out);
  not not_22 (not_22_out, X3);
  and and_16 (and_16_out, X1, X3);
  not not_23 (not_23_out, X2);
  and and_17 (and_17_out, not_23_out, X3);
  not not_24 (not_24_out, X1);
  and and_18 (and_18_out, not_24_out, X2, not_25_out);
  not not_25 (not_25_out, X3);
  not not_26 (not_26_out, X0);
  and and_19 (and_19_out, not_26_out, X1);
  and and_20 (and_20_out, X1, not_27_out);
  not not_27 (not_27_out, X2);
  and and_21 (and_21_out, X0, X3);
  not not_28 (not_28_out, X0);
  and and_22 (and_22_out, not_28_out, not_29_out);
  not not_29 (not_29_out, X2);
  and and_23 (and_23_out, X2, X3);
  not not_30 (not_30_out, X0);
  and and_24 (and_24_out, not_30_out, X1);
  and and_25 (and_25_out, X1, X3);
  not not_31 (not_31_out, X0);
  not not_32 (not_32_out, X2);
  and and_26 (and_26_out, not_31_out, not_32_out, not_33_out);
  not not_33 (not_33_out, X3);
  not not_34 (not_34_out, X1);
  and and_27 (and_27_out, not_34_out, X3);
  not not_35 (not_35_out, X0);
  and and_28 (and_28_out, not_35_out, X1, X2);
  not not_36 (not_36_out, X1);
  and and_29 (and_29_out, X0, not_36_out, X2);
  and and_30 (and_30_out, X0, X1, not_37_out);
  not not_37 (not_37_out, X2);
  not not_38 (not_38_out, X3);
  and and_31 (and_31_out, not_38_out, not_39_out);
  not not_39 (not_39_out, X1);
  not not_40 (not_40_out, X3);
  and and_32 (and_32_out, not_40_out, X0);
  not not_41 (not_41_out, X1);
  and and_33 (and_33_out, not_41_out, X0);
  not not_42 (not_42_out, X3);
  and and_34 (and_34_out, not_42_out, X2);
  and and_35 (and_35_out, X3, not_43_out);
  not not_43 (not_43_out, X2);
  or or_1 (A, and_1_out, and_2_out, and_3_out, and_4_out, and_5_out);
  or or_2 (C, and_12_out, and_13_out, and_14_out, and_15_out, and_16_out);
  or or_3 (D, and_17_out, and_18_out, and_19_out, and_20_out, and_21_out);
  or or_4 (E, and_22_out, and_23_out, and_24_out, and_25_out);
  or or_5 (F, and_26_out, and_27_out, and_28_out, and_29_out, and_30_out);
  or or_6 (G, and_31_out, and_32_out, and_33_out, and_34_out, and_35_out);
  or or_7 (B, and_6_out, and_7_out, and_8_out, and_9_out, and_10_out, and_11_out);

  assign H = 1'b0;
endmodule
